// Digital circuit BW8cpu.dig as structural Verilog
module BW8cpu (
  input  VCC,
  input  GND,
  input  nIRQ,
  input  nREQ,
  input  crystal,
  input  _555,
  input  step,
  output [15:0] ADDR,
  output R_nW,
  output nACK,
  output nBRK
);

  wire a_dbus_a, a_dbus_l, a_lhs_a, a_rhs_a, alu_dbus_a, alu_res, b_dbus_a, b_dbus_l, b_lhs_a, b_rhs_a,
       c_dbus_a, c_dbus_l, c_lhs_a, c_rhs_a, clk, clk_crystal, d_dbus_a, d_dbus_l, d_lhs_a, d_rhs_a, dec_sp,
       dp_addr_a, dp_dbus_a, dp_dbus_l, dpi_dbus_a, e_addr_a, e_xfer_l, ext, ir_dbus_l, isr_xfer_a,
       mem_dbus_a, mem_dbus_l, nclk, nirq_latched, nrst, nRST_out, pc_addr_a, pc_inc, pc_xfer_a, pc_xfer_l,
       reg_pc, reg_sp, reg_x, reg_y, rst, rst_latched, rst_xfer_a, sp_addr_a, sp_dec, sp_inc, sp_xfer_a,
       sp_xfer_l, spi_xfer_a, sr_dbus_a, sr_dbus_l, t1_dbus_a, t1_dbus_l, t1_rhs_a, t2_dbus_a, t2_dbus_l,
       t2_lhs_a, t_addr_a, t_inc, x_addr_a, x_dec, x_inc, x_xfer_a, x_xfer_l, y_addr_a, y_dec, y_inc,
       y_xfer_a, y_xfer_l, zero_dbus_a;
  wire [2:0] addr_a, Break_out, count, t_state, triple_clock_1_p9, xfer_l;
  wire [3:0] dbus_a, dbus_l;
  wire [4:0] alu_op, flags, xfer_a;
  wire [7:0] dbus, lhs, opcode, reg_a, reg_b, reg_c, reg_d, reg_dp, reg_t1, reg_t2, rhs;
  wire [15:0] addr_bus, xfer;

  // Probe on dbus
  // Probe on xfer
  // Probe on ADDR
  // Probe on 8'hbb
  // Probe on reg_a
  // Probe on reg_b
  // Probe on reg_c
  // Probe on reg_d
  // Probe on reg_dp
  // Probe on reg_t2
  // Probe on alu_res
  PowerSupply powersupply_1 (.VDD(VCC), .GND(GND));
  // Probe on reg_pc
  // Probe on reg_sp
  // Probe on reg_x
  // Probe on reg_y
  // Probe on reg_t1
  // Probe on rst_latched
  // Probe on nirq_latched
  // Probe on opcode
  // Probe on ext
  // Probe on flags
  control_unit Control_Unit (
    .nirq(nIRQ), .opcode(opcode), .flags(flags), .nreq(nREQ), .clk(clk), .nrst(nrst), .dbus_assert(dbus_a),
    .dbus_load(dbus_l), .alu_op(alu_op), .xfer_assert(xfer_a), .xfer_load(xfer_l), .addr_assert(addr_a),
    .count(count), .dec_sp(dec_sp), .nbrk(nBRK), .nclk(nclk), .rst(rst),
    .dbg({rst_latched, nirq_latched, ext, opcode, flags, t_state}));
  instruction_register Instruction_Register (
    .clk(clk), .dbus(dbus), .dbus_load(ir_dbus_l), .clr(nrst), .opcode(opcode));
  constant_generator_8bit DP_Initial_Val (
    .dpi_dbus_assert(dpi_dbus_a), .DPi(8'h1), .zero_dbus_assert(zero_dbus_a), .dbus(dbus));
  memory_bridge Memory_Bridge (.dbus_assert(mem_dbus_a), .dbus_load(mem_dbus_l), .dbus(dbus), .mbus(8'hbb));
  reset_module reset_module_1 (.clk(clk_crystal), .nrst_in(nRST_out), .nrst(nrst));
  Button u_nRST (.out(nRST_out));
  Button #(.activeLow("true")) Run (.out(Break_out[0]));
  Button #(.activeLow("true")) Demo (.out(Break_out[1]));
  Button #(.activeLow("true")) Break (.out(Break_out[2]));
  // Probe on t_state
  // triple_clock triple_clock_1: pin names not known; wires that end beside it: Break_out, nBRK, {nrst, 2'b11}, crystal, _555, step, clk, clk_crystal, triple_clock_1_p9
  // Probe on rst
  // Probe on nclk
  LED u_crystal (.in(clk_crystal));
  // Probe on dec_sp
  // Probe on nBRK
  LED cpu (.in(clk));
  LED Run_Mode_Active (.in(triple_clock_1_p9[0]));
  LED Demo_Mode_Active (.in(triple_clock_1_p9[1]));
  LED Break_Mode_Active (.in(triple_clock_1_p9[2]));
  // Probe on count
  // Probe on addr_a
  // Probe on xfer_l
  // Probe on xfer_a
  bus_controller Bus_Controller (
    .dbus_assert(dbus_a), .dbus_load(dbus_l), .xfer_assert(xfer_a), .xfer_load(xfer_l), .addr_assert(addr_a),
    .clk(clk), .count(count), .dec_sp(dec_sp), .nclk(nclk), .ALU_dbus_assert(alu_dbus_a),
    .A_dbus_assert(a_dbus_a), .B_dbus_assert(b_dbus_a), .C_dbus_assert(c_dbus_a), .D_dbus_assert(d_dbus_a),
    .SR_dbus_assert(sr_dbus_a), .DP_dbus_assert(dp_dbus_a), .T1_dbus_assert(t1_dbus_a),
    .T2_dbus_assert(t2_dbus_a), .MEM_dbus_load(mem_dbus_l), .A_dbus_load(a_dbus_l), .B_dbus_load(b_dbus_l),
    .C_dbus_load(c_dbus_l), .D_dbus_load(d_dbus_l), .SR_dbus_load(sr_dbus_l), .DP_dbus_load(dp_dbus_l),
    .T1_dbus_load(t1_dbus_l), .T2_dbus_load(t2_dbus_l), .A_lhs_assert(a_lhs_a), .B_lhs_assert(b_lhs_a),
    .C_lhs_assert(c_lhs_a), .D_lhs_assert(d_lhs_a), .A_rhs_assert(a_rhs_a), .B_rhs_assert(b_rhs_a),
    .C_rhs_assert(c_rhs_a), .D_rhs_assert(d_rhs_a), .PC_xfer_assert(pc_xfer_a), .SP_xfer_assert(sp_xfer_a),
    .X_xfer_assert(x_xfer_a), .Y_xfer_assert(y_xfer_a), .ISR_xfer_assert(isr_xfer_a),
    .RST_xfer_assert(rst_xfer_a), .PC_xfer_load(pc_xfer_l), .SP_xfer_load(sp_xfer_l), .X_xfer_load(x_xfer_l),
    .Y_xfer_load(y_xfer_l), .E_xfer_load(e_xfer_l), .PC_addr_assert(pc_addr_a), .SP_addr_assert(sp_addr_a),
    .X_addr_assert(x_addr_a), .Y_addr_assert(y_addr_a), .E_addr_assert(e_addr_a), .DP_addr_assert(dp_addr_a),
    .MEM_dbus_assert(mem_dbus_a), .IR_dbus_load(ir_dbus_l), .T1_rhs_assert(t1_rhs_a), .PC_inc(pc_inc),
    .SP_inc(sp_inc), .X_inc(x_inc), .Y_inc(y_inc), .SP_dec(sp_dec), .X_dec(x_dec), .Y_dec(y_dec),
    .DPI_dbus_assert(dpi_dbus_a), .SPI_xfer_assert(spi_xfer_a), .T_addr_assert(t_addr_a),
    .ACK_addr_assert(nACK), .T_inc(t_inc), .T2_lhs_assert(t2_lhs_a), .zero_dbus_assert(zero_dbus_a));
  // Probe on alu_op
  // Probe on dbus_l
  // Probe on dbus_a
  general_purpose_register C_Register (
    .clk(c_dbus_l), .dbus_load(c_dbus_a), .dbus_assert(c_lhs_a), .lhs_assert(c_rhs_a), .rhs_assert(nrst),
    .clr(dbus[0]), .lhs(lhs), .rhs(rhs), .\reg (reg_c));  // open: dbus
  alu Arithmetic___Logic_Unit_and_Status_Register (
    .ALU_OP(alu_op), .LOAD_SR_DBUS(sr_dbus_l), .ASSERT_SR_DBUS(sr_dbus_a), .CLK(clk), .CLR(rst), .LHS(lhs),
    .RHS(rhs), .ASSERT_ALU_DBUS(alu_dbus_a));  // open: FLAGS, DBUS, q
  accumulator E_Accumulator__A___B (
    .addr_assert(e_addr_a), .xfer_load(e_xfer_l), .a_dbus_load(a_dbus_l), .b_dbus_load(b_dbus_l),
    .a_dbus_assert(a_dbus_a), .b_dbus_assert(b_dbus_a), .a_lhs_assert(a_lhs_a), .b_lhs_assert(b_lhs_a),
    .a_rhs_assert(a_rhs_a), .b_rhs_assert(b_rhs_a), .dbus(dbus), .xfer(xfer), .clk(nrst), .addr(addr_bus),
    .reg_a(reg_a), .reg_b(reg_b));  // open: clr
  direct_page_register DP___Temp_Register (
    .dbus(dbus), .clk(clk), .clr(rst), .assert_dp_addr(dp_addr_a), .assert_t1_dbus(t1_dbus_a),
    .assert_t1_rhs(t1_rhs_a), .assert_dp_dbus(dp_dbus_a), .load_t1_dbus(t1_dbus_l), .load_dp_dbus(dp_dbus_l),
    .load_t2_dbus(t1_dbus_l), .assert_t_addr(t_addr_a), .assert_t2_dbus(t2_dbus_a), .assert_t2_lhs(t2_lhs_a),
    .t_inc(t_inc), .nclr(nrst), .reg_dp(reg_dp), .reg_t1(reg_t1), .reg_t2(reg_t2), .xfer(xfer), .addr(ADDR));
  general_purpose_register D_Register (
    .clk(d_dbus_l), .dbus_load(d_dbus_a), .dbus_assert(d_lhs_a), .lhs_assert(d_rhs_a), .rhs_assert(nrst),
    .clr(dbus[0]), .lhs(lhs), .rhs(rhs), .\reg (reg_d));  // open: dbus
  // address_register Program_Counter: pin names not known; wires that end beside it: flags, dbus, alu_res, xfer, rst, pc_xfer_l, pc_addr_a, pc_xfer_a, pc_inc, 1'b1, clk, ADDR, reg_pc
  // address_register Stack_Pointer: pin names not known; wires that end beside it: xfer, rst, sp_xfer_l, sp_addr_a, sp_xfer_a, sp_inc, sp_dec, clk, ADDR, reg_sp
  // address_register X_Index: pin names not known; wires that end beside it: xfer, rst, x_xfer_l, x_addr_a, x_xfer_a, x_inc, x_dec, clk, ADDR, reg_x
  // address_register Y_Index: pin names not known; wires that end beside it: xfer, rst, y_xfer_l, y_addr_a, y_xfer_a, y_inc, y_dec, clk, ADDR, reg_y
  constant_generator_16bit RST_Vector_Hi__ISR_Vector_Hi__and_SP_Init_Val (
    .RSTv_Lo(16'h100), .ISRv_Lo(16'hfe), .SPi(16'h7fff), .SPi_xfer_assert(spi_xfer_a),
    .RST_xfer_assert(rst_xfer_a), .ISR_xfer_assert(isr_xfer_a), .xfer(xfer));
  // Pins of 1 and 8 bits meet at dbus

  assign R_nW = 1'b0;

  // Other names for the same wires on the sheet: ack_addr_a = nACK; clk_cpu = clk; rst_clk_mode[2] = nrst

  // Notes on the sheet:
  //   VCC: default 1
  //   nIRQ: default 1
  //   nREQ: default 1
  //   crystal: Hz: 5
  //   External Pinout
  //   Buses & Constants
  //   Registers
endmodule
