// Digital circuit bus_controller.dig as structural Verilog
module bus_controller (
  input  [3:0] DBUS_ASSERT,
  input  [3:0] DBUS_LOAD,
  input  [4:0] XFER_ASSERT,
  input  [1:0] XFER_LOAD,
  input  [2:0] ADDR_ASSERT,
  output A_DBUS_ASSERT,
  output B_DBUS_ASSERT,
  output C_DBUS_ASSERT,
  output D_DBUS_ASSERT,
  output ALU_DBUS_ASSERT,
  output SR_DBUS_ASSERT,
  output DP_DBUS_ASSERT,
  output ZP_DBUS_ASSERT,
  output TEMP_DBUS_ASSERT,
  output MEM_DBUS_LOAD,
  output A_DBUS_LOAD,
  output B_DBUS_LOAD,
  output C_DBUS_LOAD,
  output D_DBUS_LOAD,
  output SR_DBUS_LOAD,
  output MEM_DBUS_ASSERT,
  output DP_DBUS_LOAD,
  output ZP_DBUS_LOAD,
  output TEMP_DBUS_LOAD,
  output IR_DBUS_LOAD,
  output A_LHS_ASSERT,
  output B_LHS_ASSERT,
  output C_LHS_ASSERT,
  output D_LHS_ASSERT,
  output A_RHS_ASSERT,
  output B_RHS_ASSERT,
  output C_RHS_ASSERT,
  output D_RHS_ASSERT,
  output PC_XFER_ASSERT,
  output SP_XFER_ASSERT,
  output X_XFER_ASSERT,
  output Y_XFER_ASSERT,
  output E_XFER_ASSERT,
  output ISR_XFER_ASSERT,
  output RST_XFER_ASSERT,
  output PC_XFER_LOAD,
  output SP_XFER_LOAD,
  output X_XFER_LOAD,
  output Y_XFER_LOAD,
  output E_XFER_LOAD,
  output PC_ADDR_ASSERT,
  output SP_ADDR_ASSERT,
  output X_ADDR_ASSERT,
  output Y_ADDR_ASSERT,
  output E_ADDR_ASSERT,
  output ZPG_ADDR_ASSERT
);

  wire addr_a0, addr_a1, addr_a2, addr_a3, addr_a4, addr_a5, addr_a6, addr_a7, dbus_a0, dbus_a1, dbus_a2,
       dbus_a3, dbus_a4, dbus_a5, dbus_a6, dbus_a7, dbus_a8, dbus_a9, dbus_a10, dbus_a11, dbus_a13, dbus_a14,
       dbus_a15, dbus_l0, dbus_l1, dbus_l2, dbus_l3, dbus_l4, dbus_l5, dbus_l6, dbus_l7, dbus_l8, dbus_l9,
       dbus_l10, dbus_l11, dbus_l12, dbus_l13, dbus_l14, dbus_l15, xfer_a0, xfer_a1, xfer_a2, xfer_a3,
       xfer_a4, xfer_a5, xfer_a6, xfer_a7, xfer_a8, xfer_a9, xfer_a10, xfer_a11, xfer_a12, xfer_a13,
       xfer_a14, xfer_a15, xfer_a16, xfer_a17, xfer_a18, xfer_a19, xfer_a20, xfer_a21, xfer_a22, xfer_a23,
       xfer_a24, xfer_a25, xfer_a26, xfer_a27, xfer_a28, xfer_a29, xfer_a30, xfer_a31, xfer_l0, xfer_l1,
       xfer_l2, xfer_l3;

  Decoder #(.Selector_Bits(4)) decoder_1 (
    .sel(DBUS_ASSERT), .out_0(dbus_a0), .out_1(dbus_a1), .out_2(dbus_a2), .out_3(dbus_a3), .out_4(dbus_a4),
    .out_5(dbus_a5), .out_6(dbus_a6), .out_7(dbus_a7), .out_8(dbus_a8), .out_9(dbus_a9), .out_10(dbus_a10),
    .out_11(dbus_a11), .out_12(dbus_a11), .out_13(dbus_a13), .out_14(dbus_a14), .out_15(dbus_a15));
  Decoder #(.Selector_Bits(4)) decoder_2 (
    .sel(DBUS_LOAD), .out_0(dbus_l0), .out_1(dbus_l1), .out_2(dbus_l2), .out_3(dbus_l3), .out_4(dbus_l4),
    .out_5(dbus_l5), .out_6(dbus_l6), .out_7(dbus_l7), .out_8(dbus_l8), .out_9(dbus_l9), .out_10(dbus_l10),
    .out_11(dbus_l11), .out_12(dbus_l12), .out_13(dbus_l13), .out_14(dbus_l14), .out_15(dbus_l15));
  Decoder #(.Selector_Bits(5)) decoder_3 (
    .sel(XFER_ASSERT), .out_0(xfer_a0), .out_1(xfer_a1), .out_2(xfer_a2), .out_3(xfer_a3), .out_4(xfer_a4),
    .out_5(xfer_a5), .out_6(xfer_a6), .out_7(xfer_a7), .out_8(xfer_a8), .out_9(xfer_a9), .out_10(xfer_a10),
    .out_11(xfer_a11), .out_12(xfer_a12), .out_13(xfer_a13), .out_14(xfer_a14), .out_15(xfer_a15),
    .out_16(xfer_a16), .out_17(xfer_a17), .out_18(xfer_a18), .out_19(xfer_a19), .out_20(xfer_a20),
    .out_21(xfer_a21), .out_22(xfer_a22), .out_23(xfer_a23), .out_24(xfer_a24), .out_25(xfer_a25),
    .out_26(xfer_a26), .out_27(xfer_a27), .out_28(xfer_a28), .out_29(xfer_a29), .out_30(xfer_a30),
    .out_31(xfer_a31));
  Decoder #(.Selector_Bits(2)) decoder_4 (
    .sel(XFER_LOAD), .out_0(xfer_l0), .out_1(xfer_l1), .out_2(xfer_l2), .out_3(xfer_l3));
  Decoder #(.Selector_Bits(3)) decoder_5 (
    .sel(ADDR_ASSERT), .out_0(addr_a0), .out_1(addr_a1), .out_2(addr_a2), .out_3(addr_a3), .out_4(addr_a4),
    .out_5(addr_a5), .out_6(addr_a6), .out_7(addr_a7));

  // Other names for the same wires on the sheet: addr_a[2:0] = ADDR_ASSERT; dbus_a[3:0] = DBUS_ASSERT;
  //   dbus_a12 = dbus_a11; dbus_l[3:0] = DBUS_LOAD; xfer_a[4:0] = XFER_ASSERT; xfer_l[1:0] = XFER_LOAD
endmodule
