// Digital circuit control_unit.dig as structural Verilog
module control_unit (
  input  nirq,
  input  [7:0] opcode,
  input  [4:0] flags,
  input  nreq,
  input  clk,
  input  nrst,
  input  nnmi,
  output [3:0] dbus_assert,
  output [4:0] dbus_load,
  output [3:0] alu_op,
  output [4:0] xfer_assert,
  output [2:0] xfer_load,
  output [2:0] addr_assert,
  output [2:0] count,
  output dec_sp,
  output nclk,
  output noffset,
  output rst,
  output [17:0] dbg
);

  wire and_1_out, and_2_out, and_3_out, and_4_out, clk_inverter_p4, clk_inverter_p5, clk_inverter_p6,
       nirq_latch, nnmi_latch, not_1_out, not_2_out, not_3_out, not_4_out, offset, or_2_out, or_4_out,
       rst_useq, sequencer_p1, sequencer_p4, sequencer_p5, sequencer_p6, set_ext;
  wire [7:0] State_Latch_q, ucode0_d, ucode1_d, ucode2_d, ucode3_d;
  wire [7:7] _74ls273_4_q;

  not not_1 (not_1_out, nreq);
  not not_2 (not_2_out, nirq);
  not not_3 (not_3_out, nnmi);
  // _7404 clk_inverter: pin names not known; wires that end beside it: clk, nrst, offset, clk_inverter_p4, clk_inverter_p5, clk_inverter_p6, 1'b1, 1'b0, nclk, rst, noffset
  // NotConnected on clk_inverter_p4
  // NotConnected on clk_inverter_p5
  // NotConnected on clk_inverter_p6
  _74ls273 State_Latch (
    .CP(nclk), .nMR(nrst), .D({3'b000, nnmi, nirq, 3'b000}), .VCC(1'b1), .GND(1'b0),
    .Q({State_Latch_q[7:5], nnmi_latch, nirq_latch, State_Latch_q[2:0]}));
  and and_1 (and_1_out, not_2_out, flags[4]);
  and and_2 (and_2_out, not_3_out, 1'b0);
  not not_4 (not_4_out, and_2_out);
  and and_3 (and_3_out, and_1_out, not_4_out);
  or or_1 (dbg[17], not_1_out, and_3_out);
  or or_2 (or_2_out, rst_useq, rst);
  or or_3 (dbg[16], not_1_out, and_2_out);
  and and_4 (and_4_out, dbg[0], dbg[1], dbg[2]);
  // _74193 sequencer: pin names not known; wires that end beside it: sequencer_p1, 1'b1, nclk, sequencer_p4, sequencer_p5, sequencer_p6, or_2_out, 1'b1, 1'b1, 1'b0, dbg[0], dbg[1], dbg[2]
  // NotConnected on sequencer_p1
  // NotConnected on sequencer_p4
  // NotConnected on sequencer_p5
  // NotConnected on sequencer_p6
  or or_4 (or_4_out, or_2_out, and_4_out);
  RS_FF_AS rs_ff_as_1 (.S(set_ext), .R(or_4_out), .Q(dbg[15]));  // open: nQ
  ROM #(.AddrBits(18), .Bits(8)) ucode0 (.A({dbg[17:15], opcode, flags[3:0], dbg[2:0]}), .sel(1'b1), .D(ucode0_d));
  ROM #(.AddrBits(18), .Bits(8)) ucode1 (.A({dbg[17:15], opcode, flags[3:0], dbg[2:0]}), .sel(1'b1), .D(ucode1_d));
  ROM #(.AddrBits(18), .Bits(8)) ucode2 (.A({dbg[17:15], opcode, flags[3:0], dbg[2:0]}), .sel(1'b1), .D(ucode2_d));
  ROM #(.AddrBits(18), .Bits(8)) ucode3 (.A({dbg[17:15], opcode, flags[3:0], dbg[2:0]}), .sel(1'b1), .D(ucode3_d));
  _74ls273 _74ls273_1 (.CP(clk), .nMR(nrst), .D(ucode0_d), .VCC(1'b1), .GND(1'b0), .Q({alu_op, dbus_assert}));
  _74ls273 _74ls273_2 (.CP(clk), .nMR(nrst), .D(ucode1_d), .VCC(1'b1), .GND(1'b0), .Q({addr_assert, dbus_load}));
  _74ls273 _74ls273_3 (.CP(clk), .nMR(nrst), .D(ucode2_d), .VCC(1'b1), .GND(1'b0), .Q({xfer_load, xfer_assert}));
  _74ls273 _74ls273_4 (
    .CP(clk), .nMR(nrst), .D(ucode3_d), .VCC(1'b1), .GND(1'b0),
    .Q({_74ls273_4_q[7], offset, set_ext, rst_useq, dec_sp, count}));

  assign dbg[14:3] = {opcode, flags[3:0]};

  // Other names for the same wires on the sheet: t_state[2:0] = dbg[2:0];
  //   ucode_addr[17:0] = {dbg[17:15], opcode, flags[3:0], dbg[2:0]}; ext = dbg[15]; C_f = flags[0]; Z_f = flags[1];
  //   V_f = flags[2]; N_f = flags[3]; I_f = flags[4]; m_0 = dbg[16]; m_1 = dbg[17]

  // Notes on the sheet:
  //   nirq: default 1
  //   nreq: default 1
  //   nnmi: default 1
  //   ucode0 loads microcode0.bin
  //   ucode1 loads microcode1.bin
  //   ucode2 loads microcode2.bin
  //   ucode3 loads microcode3.bin
endmodule
